# Fritzing sketch desenho1 (saved by Fritzing 0.9.3b)
breadboards: 1

parts:
  Componente1 = Arduino Uno (Rev3)  # not connected
  Componente2 = Rotoshield - Motor driver shield for Arduino
  M1 = Stepper Motor - Bipolar
  M2 = Stepper Motor - Bipolar

nets:
  N1: Componente2.M1-2, M1.B
  N2: Componente2.M1-1, M1.A
  N3: Componente2.M2-2, M1.D
  N4: Componente2.M2-1, M1.C
  N5: Componente2.M3-2, M2.B
  N6: Componente2.M3-1, M2.A
  N7: Componente2.M4-2, M2.D
  N8: Componente2.M4-1, M2.C
